# Fritzing sketch fritzing_schema (saved by Fritzing 1.0.5)
stripboards: 3

parts:
  DHT1 = DHT22 Humidity and Temperature Sensor
  Part1 = Adafruit SCD4x [part_number="Adafruit #5187"]
  Part2 = Adafruit PMSA003I Air Quality Breakout [part_number="Adafruit #4632"]
  A1 = Raspberry Pi 5
  R1 = Resistor [tolerance=±5% power=0.25W resistance=220 package=THT]
  SG1 = Buzzer 12mm [part_number=COM-07950 package=buzzer-12mm-ns]

nets:
  VCC: DHT1.VDD, Part1.VCC, Part2.VCC, A1.5V, A1.Fan-5V, R1.Pin_0
  N1: DHT1.DATA, A1.GPIO4, R1.Pin_1
  GND: DHT1.GND, Part1.GND, Part2.GND, A1.GND, A1.Fan-GND, SG1.2
  N2: Part1.SCL, Part2.SCL, A1.GPIO18
  N3: Part1.SDA, Part2.SDA, A1.GPIO2
  N4: A1.GPIO23, SG1.1

notes:
  1) Red (+5V)
  2) Black (GND)
  3) Yellow (Clock)
  4) Orange (I2C DATA)
  5) Green (GPIO)
  10k

custom parts:
  Adafruit SCD4x: Take a deep breath in...now slowly breathe out. Mmm isn't it wonderful? All that air around us, which we bring into our lungs, extracts oxygen from and then breathes out carbon dioxide. CO2 is essential for life on this planet we call Earth - we and plants take turns using and emitting CO2 in an elegant symbiosis. But it's important to keep that CO2 balanced - you don't want too much around,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
  Adafruit PMSA003I Air Quality Breakout: Breathe easy, knowing that you can track and sense the quality of the air around you with this Adafruit PMSA003I Air Quality Breakout. This sensor is great for monitoring air quality, in a compact plug-in format. Best of all, unlike almost all other sensors we've seen that are UART interface, this one is I2C interface, which makes it a great match for single board Linux computers like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
  Raspberry Pi 5: The RPi5, a faster version of the awesome Raspberry Pi4B ARM Board with 40 pin gpio.
  Buzzer 12mm: Buzzer 12mm Spark Fun Electronics SKU : Comp-Buzzer Through hole This is a small 12mm round speaker that operates around the audible 2kHz range. You can use these speakers to create simple music or user interfaces. This is not a true piezoelectric speaker but behaves similarly. Instead of a piezoelectric crystal that vibrates with an electric current, this tiny speaker uses an electromagnet to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
